// Logisim project Converter.circ as structural Verilog: 1 circuit, main circuit main
module main (
  input  [3:0] in_1,
  output [3:0] out_2
);

  wire not_1_out, not_2_out, not_3_out, not_4_out, or_1_out, or_2_out, or_3_out, or_4_out, or_5_out, or_6_out;

  not not_1 (not_1_out, in_1[0]);
  or or_1 (or_1_out, in_1[3], in_1[1], not_1_out);
  and and_1 (out_2[0], or_1_out, or_2_out);
  not not_2 (not_2_out, in_1[0]);
  or or_2 (or_2_out, in_1[3], in_1[2], not_2_out);
  not not_3 (not_3_out, in_1[1]);
  not not_4 (not_4_out, in_1[0]);
  or or_3 (or_3_out, in_1[3], in_1[2], not_3_out, not_4_out);
  or or_4 (or_4_out, in_1[3], in_1[1], in_1[0]);
  and and_2 (out_2[1], or_3_out, or_4_out);
  or or_5 (or_5_out, in_1[3], in_1[2], in_1[0]);
  and and_3 (out_2[2], or_5_out, or_6_out);
  or or_6 (or_6_out, in_1[3], in_1[2], in_1[1]);

  assign out_2[3] = 1'b1;
endmodule
